# Fritzing sketch Schaltplan (saved by Fritzing 0.9.6b)

parts:
  Raspi = Raspberry Pi 4B
  VALVE1 = Plastic Solenoid Valve
  Relais = KY-019 5V Relay Module [package="Breakout board"]
  J1 = single row smd female pin header, 7 pins [form="♀ (female)"]
  12V = Power Jack [package=power_jack_smd]

nets:
  N1: Raspi.5V, Relais.+
  N2: Raspi.GPIO5, Relais.S
  N3: Raspi.GND, Relais.-
  N4: Raspi.GPIO6, J1.pin1
  N5: Raspi.GPIO13, J1.pin2
  N6: Raspi.GPIO19, J1.pin3
  N7: Raspi.GPIO16, J1.pin7
  N8: Raspi.GPIO26, J1.pin4
  N9: Raspi.GPIO20, J1.pin6
  N10: Raspi.GPIO21, J1.pin5
  N11: VALVE1.no_name_yet#1, Relais.NO
  N12: VALVE1.no_name_yet#2, 12V.GND
  N13: Relais.Common, 12V.PWR

custom parts:
  KY-019 5V Relay Module: KY-019 5V Relay module, used to control AC circuits. (Special thanks to vanepp for fixing the PCB holes and other errors)
